# Fritzing sketch IrRelayRestServer (saved by Fritzing 0.9.3b)
breadboards: 1

parts:
  パーツ1 = Arduino Ethernet Shield (Rev3)
  パーツ2 = Arduino Mega 2560 (Rev3)  # not connected
  Grove3 = Grove Infrared Emitter

nets:
  N1: パーツ1.SDCS, Grove3.TX
  5V: パーツ1.5V, Grove3.VCC
  GND: パーツ1.GND, Grove3.GND
