# Fritzing sketch Bluetoothドングル版 (saved by Fritzing 0.9.2b)
breadboards: 1

parts:
  パーツ1 = Arduino Mega ADK (Rev3)
  RTC1 = RTC-8564NB [package="Module(DIP 8P)"]
  DHT1 = DHT22 Humidity and Temperature Sensor
  R1 = Resistor [tolerance=±5% resistance=10k package="1206 [SMD]"]

nets:
  N1: パーツ1.D21/SCL, RTC1.SCL
  N2: パーツ1.D20/SDA, RTC1.SDA
  N3: パーツ1.D18/TX1, RTC1.INT
  GND: パーツ1.GND, RTC1.GND, DHT1.GND
  VDD: パーツ1.IOREF, パーツ1.5V, RTC1.VDD, DHT1.VDD, R1.Pin_0
  N4: パーツ1.D4_PWM, DHT1.DATA, R1.Pin_1

custom parts:
  RTC-8564NB: Real Time Clock Module and I2C-BUS interface method. This product is a module of the SON 8-pin DIP package. Supply voltage 1.8-5.5V

// code stored in the sketch: Dht22RtcSpp.ino
file:///C:/Users/noro/Desktop/Dht22RtcSpp.ino//
// DHT????????????????????Bluetooth??????????
// RTC???????????????????????
// ??????????Arduino???????????
// RTC????????????
//

//#define USE_SERIAL
#define USE_RTC


//
// USB????????Bluetooth??????????
//

#include <SPP.h>
//#include <usbhub.h>

// Satisfy the IDE, which needs to see the include statment in the ino too.
#ifdef dobogusinclude
#include <spi4teensy3.h>
#include <SPI.h>
#endif

USB Usb;
//USBHub Hub1(&Usb); // Some dongles have a hub inside

BTD Btd(&Usb); // You have to create the Bluetooth Dongle instance like so
/* You can create the instance of the class in two ways */
SPP SerialBT(&Btd); // This will set the name to the defaults: "Arduino" and the pin to "0000"
//SPP SerialBT(&Btd, "Lauszus's Arduino", "1234"); // You can also set the name and pin like so

//
// RTC8564????????????????????????????
//
#ifdef USE_RTC
//
#include <Wire.h>
#include <skRTClib.h>
#include <avr/sleep.h>
//
// RTC??arduino???????????????????
// ???????????????????????????????????????????
//
// ????Mega2560???INT0,1???????????????????????
#define INT_NUMBER 5
#define PIN_NUMBER 18
// UNO?INT0,1??????????????
//#define INT_NUMBER 0
//#define PIN_NUMBER 2
//
//?????????????????
//
//#define STANDBY_MODE SLEEP_MODE_IDLE
//#define STANDBY_MODE SLEEP_MODE_ADC
//#define STANDBY_MODE SLEEP_MODE_PWR_SAVE
//#define STANDBY_MODE SLEEP_MODE_STANDBY
#define STANDBY_MODE SLEEP_MODE_PWR_DOWN
//
// ??????????
//
#define SLEEP_DURATION 4 //?????
//#define SLEEP_UNIT 0 // 244.14us??
//#define SLEEP_UNIT 1 //15.625ms??
//#define SLEEP_UNIT 2 //???
#define SLEEP_UNIT 3 //???
#endif /* USE_RTC */

#ifdef USE_SERIAL
#include <stdio.h>
#endif /* USE_SERIAL */

/*
 * DHT?????
 */
#include <DHT.h>
#define DHTPIN 4     // what pin we're connected to

// Uncomment whatever type you're using!
//#define DHTTYPE DHT11   // DHT 11 
#define DHTTYPE DHT22   // DHT 22  (AM2302)
//#define DHTTYPE DHT21   // DHT 21 (AM2301)

// Connect pin 1 (on the left) of the sensor to +5V
// NOTE: If using a board with 3.3V logic like an Arduino Due connect pin 1
// to 3.3V instead of 5V!
// Connect pin 2 of the sensor to whatever your DHTPIN is
// Connect pin 4 (on the right) of the sensor to GROUND
// Connect a 10K resistor from pin 2 (data) to pin 1 (power) of the sensor

// Initialize DHT sensor for normal 16mhz Arduino
DHT dht(DHTPIN, DHTTYPE);
// NOTE: For working with a faster chip, like an Arduino Due or Teensy, you
// might need to increase the threshold for cycle counts considered a 1 or 0.
// You can do this by passing a 3rd parameter for this threshold.  It's a bit
// of fiddling to find the right value, but in general the faster the CPU the
// higher the value.  The default for a 16mhz AVR is a value of 6.  For an
// Arduino Due that runs at 84mhz a value of 30 works.
// Example to initialize DHT sensor for Arduino Due:
//DHT dht(DHTPIN, DHTTYPE, 30);

//
// ??????
//
int counter=0; //??????????????????????????????
#define KELVIN 273.15 //?????????????
#define THRESHOLD 20
//
// ??????????
//
#ifdef USE_SERIAL
bool firstMessage = true;
static FILE uartout;

static int uart_putchar (char c, FILE *stream) {
  if (Serial.write(c) > 0) {
    return 0;
  } else {
    return -1;
  }
}
#endif /* USE_SERIAL */

// RTC(CLKOUT)????????????????
// loop()??????????????????????
// ???????
//
// ??????????????????????????
//
#ifdef USE_RTC
void InterRTC()
{
  RTC.InterFlag = 1 ;
#ifdef USE_SERIAL
  Serial.println("Interupt");
#endif /* USE_SERIAL */
}
#endif /* USE_RTC */

//
// ???
// USB, Bluetooth,??????????
// ??????????????????
//
void setup()
{
  int ans ;
#ifdef USE_SERIAL
  fdev_setup_stream (&uartout, uart_putchar, NULL, _FDEV_SETUP_WRITE);
  stdout = &uartout;
#endif /* USE_SERIAL */
#ifdef USE_RTC
  pinMode( PIN_NUMBER, INPUT);    // RTC?????????????
#endif /* USE_RTC */
#ifdef USE_SERIAL
  Serial.begin(9600) ;                    // ??????????
#endif /* USE_SERIAL */
#ifdef USE_RTC
  ans = RTC.begin(PIN_NUMBER,INT_NUMBER,InterRTC,12,1,10,2,15,30,0) ;  // 2012/01/10 ? 15:30:00 ?RTC??????
  if (ans == 0) {
#ifdef USE_SERIAL
    Serial.println("Successful initialization of the RTC") ;// ?????
#endif /* USE_SERIAL */
  } else {
#ifdef USE_SERIAL
    Serial.print("Failed initialization of the RTC ans=") ; // ?????
    Serial.println(ans) ;
#endif /* USE_SERIAL */
    while(1) ;                         // ????
  }
  RTC.SetTimer(SLEEP_UNIT,SLEEP_DURATION) ;
#endif /* USE_RTC */
  if (Usb.Init() == -1) {
#ifdef USE_SERIAL
    Serial.print(F("\r\nOSC did not start"));
#endif /* USE_SERIAL */
    while (1); //????
  }
#ifdef USE_SERIAL
  Serial.print(F("\r\nSPP Bluetooth Library Started"));
#endif /* USE_SERIAL */
}

//
// ???????
//
void loop()
{
  Usb.Task(); // The SPP data is actually not send until this is called, one could call SerialBT.send() directly as well
  if (SerialBT.connected) {
#ifdef USE_SERIAL
    if (firstMessage) {
      // Bluetooth??????????????????
      firstMessage = false;
      Serial.println("Bluetooth connected");
    }
#endif /* USE_SERIAL */
    float h = dht.readHumidity(); //??
    float t = dht.readTemperature(false); //??
    float hi = dht.convertFtoC(dht.computeHeatIndex(dht.convertCtoF(t),h)); //????
    if (isnan(t) || isnan(h)) {
#ifdef USE_SERIAL
      Serial.println("Failed to read from DHT");
#endif /* USE_SERIAL */
      SerialBT.println("DHT22:C:0:F:0:H:0:HI:0");
      SerialBT.flush();
    } else {
#ifdef USE_SERIAL
      Serial.print("Humidity: "); 
      Serial.print(h);
      Serial.print(" %\t");
      Serial.print("Temperature: "); 
      Serial.print(t);
      Serial.println(" *C");
      Serial.print("Heat Index : ");
      Serial.println(hi);
#endif /* USE_SERIAL */
      // //LM35:C:23.46:DHT11:C:32.00:F:89.60:H:42.00:HI:C:25.19
      // ???????????????????????
      t += KELVIN;
      hi += KELVIN;
      SerialBT.print("DHT22:K:");
      SerialBT.print(t);
      SerialBT.print(":H:");
      SerialBT.print(h);
      SerialBT.print(":HI:");
      SerialBT.println(hi);
      SerialBT.flush();
    }
    counter++;
    if (counter==THRESHOLD) {
      // ??????????????????????
      software_Reset();
    }
#ifdef USE_RTC
  goodNight(STANDBY_MODE);// ???????
  if (RTC.InterFlag == 1) {  // ??????????
    RTC.InterFlag = 0 ;                // ????????????
  }
#else /* USE_RTC */
  delay(30000);
#endif /* USE_RTC */
  } else {
#ifdef USE_SERIAL
    firstMessage = true;
#endif /* USE_SERIAL */
  }
}
//
// ????????????????
//
#ifdef USE_RTC
void goodNight(int i) {
#ifdef USE_SERIAL
  Serial.println("  Good Night");
#endif /* USE_SERIAL */
  delay(100);
  noInterrupts();
  set_sleep_mode(i);
  sleep_enable();
  interrupts();
  sleep_cpu();
  sleep_disable();
}
#endif /* USE_RTC */
//
// ???????????????????????????
// ???????????????
//
void software_Reset(){
#ifdef USE_SERIAL
  Serial.println(" RESET");
#endif /* USE_SERIAL */
  asm volatile ("  jmp 0");
}
