# Fritzing sketch circuit (saved by Fritzing 0.9.3b)
breadboards: 2

parts:
  Q1 = TRANSISTOR_NPN [part_number=2SC4081 package=to-92]
  R2 = Resistor [tolerance=±5% resistance=1k package="1206 [SMD]"]
  R1 = Resistor [tolerance=±5% resistance=10k package="1206 [SMD]"]
  U2 = ESP32-38PinWide [part_number=ESP32-38PinWide]
  Raspberry_Pi_1 = Raspberry Pi 3 [part_number=RPI-3-V1.2]
  U3 = RELAY [package=relay-jzc]
  D1 = P1000K [part_number=1SS355]

nets:
  GND: Q1.E, R1.Pin_1, U2.GND, Raspberry_Pi_1.GND, U3.NO
  N1: Q1.B, R2.Pin_0, R1.Pin_0
  N2: Q1.C, U3.COIL2, D1.anode
  N3: R2.Pin_1, U2.GPIO15
  3.3V: U2.3.3, U3.COIL1, D1.cathode
  Pi Tx: U2.GPIO16, Raspberry_Pi_1.GIPO14
  Pi Rx: U2.GPIO17, Raspberry_Pi_1.GIPO15
  N4: Raspberry_Pi_1.GPIO3, U3.MAIN

custom parts:
  ESP32-38PinWide: Generic 38-Pin ESP32 with wide format (only access to one side of pins on a breadboard) based on Stephen Lilley's HiLetgo ESP-WROOM-32 ESP32 ESP-32S Development Board.
